# Fritzing sketch Untitled Sketch (saved by Fritzing 0.9.3b)
breadboards: 1

parts:
  부품1 = Arduino Uno (Rev3)
  L298N1 = L298N DC motor driver
  VCC1 = Battery block 9V
  VCC2 = Battery block 9V
  BT1 = Bluetooth HC-06u [package=THT]
  LED1 = smd LED [color="Red (633nm)" package="1206 [SMD]"]
  R1 = Resistor [tolerance=±5% resistance=220 package="2512 [SMD]"]
  M1 = Getriebemotor
  M3 = Getriebemotor
  M4 = Getriebemotor
  M5 = Getriebemotor

nets:
  N1: 부품1.D8, L298N1.IN2
  N2: 부품1.D9_PWM, L298N1.IN1
  N3: 부품1.D10_PWM/SS, L298N1.ENA
  N4: 부품1.D11_PWM/MOSI, R1.Pin_1
  N5: 부품1.D2, BT1.TXD
  N6: 부품1.D3_PWM, BT1.RXD
  N7: 부품1.D5_PWM, L298N1.ENB
  N8: 부품1.D6_PWM, L298N1.IN4
  N9: 부품1.D7, L298N1.IN3
  5V: 부품1.5V, BT1.VCC
  GND: 부품1.GND, BT1.GND, LED1.cathode
  N10: L298N1.OUT1, M3.pin_1, M4.pin_1
  N11: L298N1.OUT2, M3.pin_2, M4.pin_2
  N12: L298N1.OUT3, M1.pin_2, M5.pin_2
  N13: L298N1.OUT4, M1.pin_1, M5.pin_1
  N14: L298N1.12V, VCC1.+
  N15: L298N1.GND, VCC2.-
  N16: VCC1.-, VCC2.+
  N17: LED1.anode, R1.Pin_0

notes:
  <-- zigzag!
  #define ENA 10
  #define ENB 5
  #define IN1 9
  #define IN2 8
  #define IN3 7
  #define IN4 6
  #define LED 11
  #define blueTx 2
  #define blueRx 3

custom parts:
  L298N DC motor driver: 2x DC motor driver with 78M05 positive voltage regulator (7..35 V) L298N: max 46 V, 2 A Set 5 V Enable jumper to enable 5 V regultor (needed for the L298N) and +5 V output at screw terminal or supply external +5 V at screw terminal Set ENA and/or ENB to +5 V to enable motor permanently or supply ENA and/or ENB with PWM signal IN1 and IN2 set rotation directory for motor A (OUT1/OUT2) IN2 and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
  Bluetooth HC-06u: Bluetooth HC-06 - face up, pins down 16.5mm x 37.5mm PCB
